// Logisim project NISC_SP25_Scaffold.circ as structural Verilog: 7 circuits, main circuit main
module main (
);

  wire nisc_cpu_1_c, nisc_cpu_1_n, nisc_cpu_1_v, nisc_cpu_1_z;
  wire [3:0] IM_data, IM_data_2, IM_data_3, nisc_cpu_1_im_address_2;
  wire [7:0] nisc_cpu_1_im_address;
  wire [11:0] nisc_cpu_1_or0;

  ROM #(.addrWidth(9), .dataWidth(12)) IM (
    .addr({nisc_cpu_1_im_address_2[0], nisc_cpu_1_im_address}), .data({IM_data_3, IM_data_2, IM_data}));
  NISC_CPU nisc_cpu_1 (
    .IM_Data({IM_data_3, IM_data_2, IM_data}),
    .IM_Address({nisc_cpu_1_im_address_2[0], nisc_cpu_1_im_address}), .N(nisc_cpu_1_n), .Z(nisc_cpu_1_z),
    .C(nisc_cpu_1_c), .V(nisc_cpu_1_v), .OR0(nisc_cpu_1_or0));
  LED led_1 (.in(nisc_cpu_1_n));
  LED led_2 (.in(nisc_cpu_1_z));
  LED led_3 (.in(nisc_cpu_1_c));
  LED led_4 (.in(nisc_cpu_1_v));
  Hex_Digit_Display hex_digit_display_1 (.value(nisc_cpu_1_im_address_2));  // open: dp
  Hex_Digit_Display hex_digit_display_2 (.value(nisc_cpu_1_im_address[7:4]));  // open: dp
  Hex_Digit_Display hex_digit_display_3 (.value(nisc_cpu_1_or0[11:8]));  // open: dp
  Hex_Digit_Display hex_digit_display_4 (.value(nisc_cpu_1_im_address[3:0]));  // open: dp
  Hex_Digit_Display hex_digit_display_5 (.value(IM_data_3));  // open: dp
  Hex_Digit_Display hex_digit_display_6 (.value(nisc_cpu_1_or0[7:4]));  // open: dp
  Hex_Digit_Display hex_digit_display_7 (.value(nisc_cpu_1_or0[3:0]));  // open: dp
  Hex_Digit_Display hex_digit_display_8 (.value(IM_data_2));  // open: dp
  Hex_Digit_Display hex_digit_display_9 (.value(IM_data));  // open: dp

  // Notes on the sheet:
  //   contents of IM (hex, n*v repeats v):
  //   c08 840 840 840 880 880 880 d00 8c0 8c0 8c0
  //   NISC
  //   SP25-Example-Demo
  //   IM Address
  //   R0 Contents
  //   IM Data
endmodule

module RegisterFile (
  input  [2:0] RA1,
  input  [2:0] RA2,
  input  [2:0] WA3,
  input  [11:0] WD3,
  input  RegW,
  input  CLK,
  input  Reset,
  output [11:0] RD1,
  output [11:0] RD2,
  output [11:0] OR0
);
endmodule

module ALU (
  input  [11:0] A,
  input  [11:0] B,
  input  [2:0] ALUOP,
  output [11:0] R,
  output N,
  output Z,
  output C,
  output V
);
endmodule

module NISC_CPU (
  input  [11:0] IM_Data,
  output [8:0] IM_Address,
  output N,
  output Z,
  output C,
  output V,
  output [11:0] OR0
);

  wire alu_1_c, alu_1_n, alu_1_v, alu_1_z, B, CLK, CVW, FlagsW, MOVC, MOVF, NZW, RegW, Reset;
  wire [2:0] undriven;
  wire [11:0] signextend6_1_s12;

  ControlUnit controlunit_1 (
    .IWord(IM_Data), .MOVC(MOVC), .MOVF(MOVF), .RegW(RegW), .FlagsW(FlagsW), .NZW(NZW), .CVW(CVW), .B(B));  // open: ALUOP
  SignExtend6 signextend6_1 (.S12(signextend6_1_s12));  // open: S6
  Hex_Digit_Display hex_digit_display_1 (.value(IM_Data[11:8]));  // open: dp
  Hex_Digit_Display hex_digit_display_2 (.value(IM_Data[7:4]));  // open: dp
  RegisterFile registerfile_1 (.OR0(OR0));  // open: RA1, RA2, WA3, WD3, RegW, CLK, Reset, RD1, RD2
  Hex_Digit_Display hex_digit_display_3 (.value(IM_Data[3:0]));  // open: dp
  Clock clock_1 (.out(CLK));
  Button u_Reset (.out(Reset));
  ALU alu_1 (.N(alu_1_n), .Z(alu_1_z), .C(alu_1_c), .V(alu_1_v));  // open: A, B, ALUOP, R
  Hex_Digit_Display hex_digit_display_4 (.value(OR0[11:8]));  // open: dp
  Hex_Digit_Display hex_digit_display_5 (.value(OR0[7:4]));  // open: dp
  Hex_Digit_Display hex_digit_display_6 (.value(OR0[3:0]));  // open: dp
  Hex_Digit_Display hex_digit_display_7 (.value({undriven, IM_Address[8]}));  // open: dp
  Hex_Digit_Display hex_digit_display_8 (.value(IM_Address[7:4]));  // open: dp
  FlagsReg flagsreg_1 (
    .N(alu_1_n), .Z(alu_1_z), .C(alu_1_c), .V(alu_1_v), .Nq(N), .Zq(Z), .Cq(C), .Vq(V));  // open: D12, NZW, CVW, FlagsW, CLK, Reset, Q12
  Hex_Digit_Display hex_digit_display_9 (.value(IM_Address[3:0]));  // open: dp
  LED led_1 (.in(N));
  LED led_2 (.in(Z));
  LED led_3 (.in(C));
  LED led_4 (.in(V));
endmodule

module SignExtend6 (
  input  [5:0] S6,
  output [11:0] S12
);
endmodule

module FlagsReg (
  input  N,
  input  Z,
  input  C,
  input  V,
  input  [11:0] D12,
  input  NZW,
  input  CVW,
  input  FlagsW,
  input  CLK,
  input  Reset,
  output Nq,
  output Zq,
  output Cq,
  output Vq,
  output [11:0] Q12
);
endmodule

module ControlUnit (
  input  [11:0] IWord,
  output MOVC,
  output MOVF,
  output RegW,
  output FlagsW,
  output NZW,
  output CVW,
  output B,
  output [2:0] ALUOP
);
endmodule
